# Fritzing sketch ControlBoard (saved by Fritzing 0.9.5d)

parts:
  Adafruit_I2C_Quad_Rotary_Encoder_Breakout1 = Adafruit I2C Quad Rotary Encoder Breakout [part_number=#5752]
  OLED_I2C1 = OLED 128x64 I2C Monochrome Display
  Adafruit_I2C_Quad_Rotary_Encoder_Breakout2 = Adafruit I2C Quad Rotary Encoder Breakout [part_number=#5752]
  Adafruit_I2C_Quad_Rotary_Encoder_Breakout3 = Adafruit I2C Quad Rotary Encoder Breakout [part_number=#5752]
  Adafruit_I2C_Quad_Rotary_Encoder_Breakout4 = Adafruit I2C Quad Rotary Encoder Breakout [part_number=#5752]
  JP1 = Header 4 [package=screwterminal-3.5mm-4_lock]

nets:
  GND: Adafruit_I2C_Quad_Rotary_Encoder_Breakout1.GND, OLED_I2C1.GND, Adafruit_I2C_Quad_Rotary_Encoder_Breakout2.GND, Adafruit_I2C_Quad_Rotary_Encoder_Breakout3.GND, Adafruit_I2C_Quad_Rotary_Encoder_Breakout4.GND, JP1.1
  VCC: Adafruit_I2C_Quad_Rotary_Encoder_Breakout1.VCC, OLED_I2C1.VDD, Adafruit_I2C_Quad_Rotary_Encoder_Breakout2.VCC, Adafruit_I2C_Quad_Rotary_Encoder_Breakout3.VCC, Adafruit_I2C_Quad_Rotary_Encoder_Breakout4.VCC, JP1.2
  N1: Adafruit_I2C_Quad_Rotary_Encoder_Breakout1.SDA, OLED_I2C1.SDA, Adafruit_I2C_Quad_Rotary_Encoder_Breakout2.SDA, Adafruit_I2C_Quad_Rotary_Encoder_Breakout3.SDA, Adafruit_I2C_Quad_Rotary_Encoder_Breakout4.SDA, JP1.3
  N2: Adafruit_I2C_Quad_Rotary_Encoder_Breakout1.SCL, OLED_I2C1.SCK, Adafruit_I2C_Quad_Rotary_Encoder_Breakout2.SCL, Adafruit_I2C_Quad_Rotary_Encoder_Breakout3.SCL, Adafruit_I2C_Quad_Rotary_Encoder_Breakout4.SCL, JP1.4

custom parts:
  Adafruit I2C Quad Rotary Encoder Breakout: Rotary encoders are soooo much fun! Twist em this way, then twist them that way. Unlike potentiometers, they go all the way around and often have little detents for tactile feedback. But, if you've ever tried to add encoders to your project you know that they're a real challenge to use: timers, interrupts, debouncing... This Stemma QT breakout makes all that frustration go away - and allows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
